# Fritzing sketch bus (saved by Fritzing 0.9.3b)
circuit board: 9.9245cm x 3.41616cm
breadboards: 1

parts:
  J18 = female pin header, 8 pins [form="♀ (female)"]
  J19 = female pin header, 8 pins [form="♀ (female)"]
  J20 = female pin header, 8 pins [form="♀ (female)"]
  J21 = female pin header, 8 pins [form="♀ (female)"]
  J22 = female pin header, 8 pins [form="♀ (female)"]
  J23 = female pin header, 8 pins [form="♀ (female)"]
  J24 = female pin header, 8 pins [form="♀ (female)"]
  J25 = female pin header, 8 pins [form="♀ (female)"]
  J26 = female pin header, 8 pins [form="♀ (female)"]
  J27 = female pin header, 8 pins [form="♀ (female)"]

nets:
  N1: J18.pin1, J19.pin1, J20.pin1, J21.pin1, J22.pin1, J23.pin1, J24.pin1, J25.pin1, J26.pin1, J27.pin1
  N2: J18.pin2, J19.pin2, J20.pin2, J21.pin2, J22.pin2, J23.pin2, J24.pin2, J25.pin2, J26.pin2, J27.pin2
  N3: J18.pin3, J19.pin3, J20.pin3, J21.pin3, J22.pin3, J23.pin3, J24.pin3, J25.pin3, J26.pin3, J27.pin3
  N4: J18.pin4, J19.pin4, J20.pin4, J21.pin4, J22.pin4, J23.pin4, J24.pin4, J25.pin4, J26.pin4, J27.pin4
  N5: J18.pin5, J19.pin5, J20.pin5, J21.pin5, J22.pin5, J23.pin5, J24.pin5, J25.pin5, J26.pin5, J27.pin5
  N6: J18.pin6, J19.pin6, J20.pin6, J21.pin6, J22.pin6, J23.pin6, J24.pin6, J25.pin6, J26.pin6, J27.pin6
  N7: J18.pin7, J19.pin7, J20.pin7, J21.pin7, J22.pin7, J23.pin7, J24.pin7, J25.pin7, J26.pin7, J27.pin7
  N8: J18.pin8, J19.pin8, J20.pin8, J21.pin8, J22.pin8, J23.pin8, J24.pin8, J25.pin8, J26.pin8, J27.pin8

notes:
  7 6 5 4 3 2 1 0
  0 1 2 3 4 5 6 7
