# Fritzing sketch RAM_v2 (saved by Fritzing 0.9.1b)
circuit board: 9.99058cm x 6.84381cm
circuit board: 9.99058cm x 9.99059cm
breadboards: 2

parts:
  GND2 = female pin header, 4 pins [form="♀ (female)"]
  VCC2 = female pin header, 4 pins [form="♀ (female)"]
  GND3 = female pin header, 4 pins [form="♀ (female)"]
  VCC3 = female pin header, 4 pins [form="♀ (female)"]
  ADDR4 = female pin header, 8 pins [form="♀ (female)"]
  ADDR5 = female pin header, 8 pins [form="♀ (female)"]
  ADDR6 = female pin header, 8 pins [form="♀ (female)"]
  ADDR7 = female pin header, 8 pins [form="♀ (female)"]
  GND = female pin header, 4 pins [form="♀ (female)"]
  VCC = female pin header, 4 pins [form="♀ (female)"]
  ADDR8 = female pin header, 8 pins [form="♀ (female)"]
  ADDR9 = female pin header, 8 pins [form="♀ (female)"]
  74245 = IC, DIP package, 20 pins [chip_label=IC]
  74LS173-H = IC, DIP package, 16 pins [chip_label=IC]
  74LS173-L = IC, DIP package, 16 pins [chip_label=IC]
  bus1 = female pin header, 8 pins [form="♀ (female)"]
  C5 = Ceramic Capacitor [capacitance=100nF package="100 mil [THT, multilayer]"]
  IS61C1024 = IC, DIP package, 32 pins [chip_label=IC]
  BANKSEL = female pin header, 3 pins [form="♀ (female)"]
  74LS74 = IC, DIP package, 14 pins [chip_label=IC]
  C6 = Ceramic Capacitor [capacitance=100nF package="100 mil [THT, multilayer]"]
  C7 = Ceramic Capacitor [capacitance=100nF package="100 mil [THT, multilayer]"]
  C8 = Ceramic Capacitor [capacitance=100nF package="100 mil [THT, multilayer]"]
  b2ram = female pin header, 1 pin [form="♀ (female)"]
  CLK = female pin header, 1 pin [form="♀ (female)"]
  ram2b = female pin header, 1 pin [form="♀ (female)"]
  CLK1 = female pin header, 1 pin [form="♀ (female)"]
  ram2b1 = female pin header, 1 pin [form="♀ (female)"]
  b2ram1 = female pin header, 1 pin [form="♀ (female)"]

nets:
  N1: GND2.pin1, GND2.pin2, GND2.pin3, GND2.pin4, GND3.pin1, GND3.pin2, GND3.pin3, GND3.pin4
  N2: VCC2.pin1, VCC2.pin2, VCC2.pin3, VCC2.pin4, VCC3.pin1, VCC3.pin2, VCC3.pin3, VCC3.pin4
  N3: ADDR4.pin1, ADDR6.pin1
  N4: ADDR4.pin2, ADDR6.pin2
  N5: ADDR4.pin3, ADDR6.pin3
  N6: ADDR4.pin4, ADDR6.pin4
  N7: ADDR4.pin5, ADDR6.pin5
  N8: ADDR4.pin6, ADDR6.pin6
  N9: ADDR4.pin7, ADDR6.pin7
  N10: ADDR4.pin8, ADDR6.pin8
  N11: ADDR5.pin1, ADDR7.pin1
  N12: ADDR5.pin2, ADDR7.pin2
  N13: ADDR5.pin3, ADDR7.pin3
  N14: ADDR5.pin4, ADDR7.pin4
  N15: ADDR5.pin5, ADDR7.pin5
  N16: ADDR5.pin6, ADDR7.pin6
  N17: ADDR5.pin7, ADDR7.pin7
  N18: ADDR5.pin8, ADDR7.pin8
  N19: GND.pin1, GND.pin2, GND.pin3, GND.pin4, 74245.pin10, 74LS173-H.pin8, 74LS173-H.pin15, 74LS173-L.pin8, 74LS173-L.pin15, C5.1, IS61C1024.pin16, IS61C1024.pin22, BANKSEL.pin1, 74LS74.pin7, C6.0, C7.0, C8.1
  N20: VCC.pin1, VCC.pin2, VCC.pin3, VCC.pin4, 74245.pin1, 74245.pin20, 74LS173-H.pin16, 74LS173-L.pin16, C5.0, IS61C1024.pin30, IS61C1024.pin32, BANKSEL.pin3, 74LS74.pin1, 74LS74.pin10, 74LS74.pin13, 74LS74.pin14, C6.1, C7.1, C8.0
  N21: ADDR8.pin1, IS61C1024.pin5
  N22: ADDR8.pin2, IS61C1024.pin6
  N23: ADDR8.pin3, IS61C1024.pin7
  N24: ADDR8.pin4, IS61C1024.pin8
  N25: ADDR8.pin5, IS61C1024.pin9
  N26: ADDR8.pin6, IS61C1024.pin10
  N27: ADDR8.pin7, IS61C1024.pin11
  N28: ADDR8.pin8, IS61C1024.pin12
  N29: ADDR9.pin1, IS61C1024.pin31
  N30: ADDR9.pin2, IS61C1024.pin3
  N31: ADDR9.pin3, IS61C1024.pin28
  N32: ADDR9.pin4, IS61C1024.pin4
  N33: ADDR9.pin5, IS61C1024.pin25
  N34: ADDR9.pin6, IS61C1024.pin23
  N35: ADDR9.pin7, IS61C1024.pin26
  N36: ADDR9.pin8, IS61C1024.pin27
  N37: 74245.pin2, 74LS173-H.pin3, IS61C1024.pin21
  N38: 74245.pin3, 74LS173-H.pin4, IS61C1024.pin20
  N39: 74245.pin4, 74LS173-H.pin5, IS61C1024.pin19
  N40: 74245.pin5, 74LS173-H.pin6, IS61C1024.pin18
  N41: 74245.pin6, 74LS173-L.pin3, IS61C1024.pin17
  N42: 74245.pin7, 74LS173-L.pin4, IS61C1024.pin15
  N43: 74245.pin8, 74LS173-L.pin5, IS61C1024.pin14
  N44: 74245.pin9, 74LS173-L.pin6, IS61C1024.pin13
  N45: 74245.pin11, 74LS173-L.pin11, bus1.pin8
  N46: 74245.pin12, 74LS173-L.pin12, bus1.pin7
  N47: 74245.pin13, 74LS173-L.pin13, bus1.pin6
  N48: 74245.pin14, 74LS173-L.pin14, bus1.pin5
  N49: 74245.pin15, 74LS173-H.pin11, bus1.pin4
  N50: 74245.pin16, 74LS173-H.pin12, bus1.pin3
  N51: 74245.pin17, 74LS173-H.pin13, bus1.pin2
  N52: 74245.pin18, 74LS173-H.pin14, bus1.pin1
  N53: 74245.pin19, IS61C1024.pin24, ram2b.pin1, ram2b1.pin1
  N54: 74LS173-H.pin1, 74LS173-H.pin2, 74LS173-L.pin1, 74LS173-L.pin2, 74LS74.pin9
  N55: 74LS173-H.pin7, 74LS173-L.pin7, 74LS74.pin3, 74LS74.pin4, 74LS74.pin11, CLK.pin1, CLK1.pin1
  N56: 74LS173-H.pin9, 74LS173-H.pin10, 74LS173-L.pin9, 74LS173-L.pin10, 74LS74.pin2, 74LS74.pin12, b2ram.pin1, b2ram1.pin1
  N57: IS61C1024.pin2, BANKSEL.pin2
  N58: IS61C1024.pin29, 74LS74.pin5
