# Fritzing sketch crystalclock (saved by Fritzing 0.9.1b)
circuit board: 12.2564cm x 5.49691cm
breadboards: 1

parts:
  XTAL = female pin header, 1 pin [form="♀ (female)"]  # not connected
  RESET = female pin header, 1 pin [form="♀ (female)"]  # not connected
  J6 = female pin header, 4 pins [form="♀ (female)"]
  J7 = female pin header, 4 pins [form="♀ (female)"]
  OUTPUT = female pin header, 1 pin [form="♀ (female)"]  # not connected
  74LS169 = IC, DIP package, 16 pins [chip_label=IC]
  C1 = Ceramic Capacitor [capacitance=100nF package="100 mil [THT, multilayer]"]
  74LS14 = IC, DIP package, 14 pins [chip_label=IC]
  C2 = Ceramic Capacitor [capacitance=100nF package="100 mil [THT, multilayer]"]
  C4 = Ceramic Capacitor [capacitance=100nF package="100 mil [THT, multilayer]"]
  RE1 = Rotary Encoder [package=THT]
  J8 = female pin header, 1 pin [form="♀ (female)"]  # not connected
  J9 = female pin header, 1 pin [form="♀ (female)"]  # not connected
  C5 = Ceramic Capacitor [capacitance=100nF package="100 mil [THT, multilayer]"]
  R1 = Resistor [tolerance=±5% resistance=14k package=THT]
  R2 = Resistor [tolerance=±5% resistance=14k package=THT]
  5161AS = 7 Segment Display
  R5 = Resistor [tolerance=±5% resistance=220 package="1206 [SMD]"]
  R6 = Resistor [tolerance=±5% resistance=220 package="1206 [SMD]"]
  R7 = Resistor [tolerance=±5% resistance=220 package="1206 [SMD]"]
  R9 = Resistor [tolerance=±5% resistance=220 package="1206 [SMD]"]
  MC14495 = IC, DIP package, 16 pins [chip_label=IC]
  R4 = Resistor [tolerance=±5% resistance=220 package="1206 [SMD]"]
  R3 = Resistor [tolerance=±5% resistance=220 package="1206 [SMD]"]
  R10 = Resistor [tolerance=±5% resistance=220 package="1206 [SMD]"]

nets:
  N1: J6.pin1, J6.pin2, 74LS169.pin3, 74LS169.pin4, 74LS169.pin5, 74LS169.pin6, 74LS169.pin7, 74LS169.pin8, 74LS169.pin10, C1.1, 74LS14.pin1, 74LS14.pin3, 74LS14.pin5, 74LS14.pin7, C2.1, C4.0, RE1.EncoderPinC, C5.1, 5161AS.common_anode, MC14495.pin7, MC14495.pin8, MC14495.pin11
  N2: J6.pin3, J6.pin4, 74LS169.pin9, 74LS169.pin16, C1.0, 74LS14.pin13, 74LS14.pin14, C2.0, R1.Pin_0, R2.Pin_0, MC14495.pin16
  N3: J7.pin1, 74LS169.pin11, MC14495.pin10
  N4: J7.pin2, 74LS169.pin12, MC14495.pin9
  N5: J7.pin3, 74LS169.pin13, MC14495.pin6
  N6: J7.pin4, 74LS169.pin14, MC14495.pin5
  N7: 74LS169.pin1, 74LS14.pin10
  N8: 74LS169.pin2, 74LS14.pin8
  N9: 74LS14.pin9, RE1.EncoderPinA, C5.0, R1.Pin_1
  N10: 74LS14.pin11, C4.1, RE1.EncoderPinB, R2.Pin_1
  N11: 5161AS.Segment_E, R7.Pin_0
  N12: 5161AS.Segment_D, R5.Pin_0
  N13: 5161AS.Segment_C, R6.Pin_0
  N14: 5161AS.Segment_B, R3.Pin_1
  N15: 5161AS.Segment_A, R4.Pin_1
  N16: 5161AS.Segment_F, R10.Pin_1
  N17: 5161AS.Segment_G, R9.Pin_1
  N18: R5.Pin_1, MC14495.pin15
  N19: R6.Pin_1, MC14495.pin14
  N20: R7.Pin_1, MC14495.pin1
  N21: R9.Pin_0, MC14495.pin3
  N22: MC14495.pin2, R10.Pin_0
  N23: MC14495.pin12, R4.Pin_0
  N24: MC14495.pin13, R3.Pin_0

notes:
  0
  1
  2
  3
  +
  -
