# Fritzing sketch regtest (saved by Fritzing 0.9.1b)
circuit board: 9.99067cm x 6.75495cm
breadboards: 1

parts:
  IC3 = IC, DIP package, 16 pins [chip_label=IC]
  IC4 = IC, DIP package, 16 pins [chip_label=IC]
  J13 = female pin header, 8 pins [form="♀ (female)"]
  J14 = female pin header, 8 pins [form="♀ (female)"]
  J15 = female pin header, 8 pins [form="♀ (female)"]
  J16 = female pin header, 8 pins [form="♀ (female)"]
  J17 = female pin header, 8 pins [form="♀ (female)"]
  J18 = female pin header, 8 pins [form="♀ (female)"]
  IC5 = IC, DIP package, 20 pins [chip_label=IC]
  J1 = female pin header, 8 pins [form="♀ (female)"]  # not connected
  IC6 = IC, DIP package, 16 pins [chip_label=IC]
  IC7 = IC, DIP package, 16 pins [chip_label=IC]
  IC8 = IC, DIP package, 20 pins [chip_label=IC]
  J19 = female pin header, 8 pins [form="♀ (female)"]
  J20 = female pin header, 8 pins [form="♀ (female)"]
  J21 = female pin header, 8 pins [form="♀ (female)"]
  J22 = female pin header, 8 pins [form="♀ (female)"]
  J23 = female pin header, 8 pins [form="♀ (female)"]
  J24 = female pin header, 8 pins [form="♀ (female)"]

nets:
  N1: IC3.pin3, J15.pin1, J17.pin1, IC5.pin9
  N2: IC3.pin4, J15.pin2, J17.pin2, IC5.pin8
  N3: IC3.pin5, J15.pin3, J17.pin3, IC5.pin7
  N4: IC3.pin6, J15.pin4, J17.pin4, IC5.pin6
  N5: IC3.pin11, IC5.pin14
  N6: IC3.pin12, IC5.pin13
  N7: IC3.pin13, IC5.pin12
  N8: IC3.pin14, IC5.pin11
  N9: IC4.pin3, J15.pin5, J17.pin5, IC5.pin5
  N10: IC4.pin4, J15.pin6, J17.pin6, IC5.pin4
  N11: IC4.pin5, J15.pin7, J17.pin7, IC5.pin3
  N12: IC4.pin6, J15.pin8, J17.pin8, IC5.pin2
  N13: IC4.pin11, IC5.pin18
  N14: IC4.pin12, IC5.pin17
  N15: IC4.pin13, IC5.pin16
  N16: IC4.pin14, IC5.pin15
  N17: J13.pin1, J18.pin1
  N18: J13.pin2, J18.pin2
  N19: J13.pin3, J18.pin3
  N20: J13.pin4, J18.pin4
  N21: J13.pin5, J18.pin5
  N22: J13.pin6, J18.pin6
  N23: J13.pin7, J18.pin7
  N24: J13.pin8, J18.pin8
  N25: J14.pin1, J16.pin1
  N26: J14.pin2, J16.pin2
  N27: J14.pin3, J16.pin3
  N28: J14.pin4, J16.pin4
  N29: J14.pin5, J16.pin5
  N30: J14.pin6, J16.pin6
  N31: J14.pin7, J16.pin7
  N32: J14.pin8, J16.pin8
  N33: IC5.pin1, IC5.pin20
  N34: IC6.pin3, IC8.pin9, J20.pin1, J23.pin1
  N35: IC6.pin4, IC8.pin8, J20.pin2, J23.pin2
  N36: IC6.pin5, IC8.pin7, J20.pin3, J23.pin3
  N37: IC6.pin6, IC8.pin6, J20.pin4, J23.pin4
  N38: IC6.pin11, IC8.pin14
  N39: IC6.pin12, IC8.pin13
  N40: IC6.pin13, IC8.pin12
  N41: IC6.pin14, IC8.pin11
  N42: IC7.pin3, IC8.pin5, J20.pin5, J23.pin5
  N43: IC7.pin4, IC8.pin4, J20.pin6, J23.pin6
  N44: IC7.pin5, IC8.pin3, J20.pin7, J23.pin7
  N45: IC7.pin6, IC8.pin2, J20.pin8, J23.pin8
  N46: IC7.pin11, IC8.pin18
  N47: IC7.pin12, IC8.pin17
  N48: IC7.pin13, IC8.pin16
  N49: IC7.pin14, IC8.pin15
  N50: IC8.pin1, IC8.pin20
  N51: J19.pin1, J21.pin1
  N52: J19.pin2, J21.pin2
  N53: J19.pin3, J21.pin3
  N54: J19.pin4, J21.pin4
  N55: J19.pin5, J21.pin5
  N56: J19.pin6, J21.pin6
  N57: J19.pin7, J21.pin7
  N58: J19.pin8, J21.pin8
  N59: J22.pin1, J24.pin1
  N60: J22.pin2, J24.pin2
  N61: J22.pin3, J24.pin3
  N62: J22.pin4, J24.pin4
  N63: J22.pin5, J24.pin5
  N64: J22.pin6, J24.pin6
  N65: J22.pin7, J24.pin7
  N66: J22.pin8, J24.pin8
